# Fritzing sketch Commander_SwitchOff_Atmega328_SIM800L (saved by Fritzing 0.9.3b)
circuit board: 11.2cm x 10.5cm
breadboards: 1

parts:
  L293D = L293D [package=THT]
  Sensor_IC = atmega328 [package=dip]
  SLOW_FAST = screw terminal, 2 pins
  D1 = Resistor [tolerance=±5% resistance=4.7k part_number=D-5819-3A package=THT]
  R8 = Resistor [tolerance=±5% resistance=3.3k package=THT]
  R7 = Resistor [tolerance=±5% resistance=10k package=THT]
  XTAL = Crystal [frequency="16 Mhz" package=THT]
  7805 = Voltage Regulator [package=to-220-alt]
  R3 = Resistor [tolerance=±5% resistance=10k package=THT]
  R4 = Resistor [tolerance=±5% resistance=3.3k package=THT]
  R5 = Resistor [tolerance=±5% resistance=10k package=THT]
  R2 = Resistor [tolerance=±5% resistance=400 package=THT]
  C5 = Ceramic Capacitor [capacitance=22pF package="100 mil [THT, multilayer]"]
  C6 = Ceramic Capacitor [capacitance=22pF package="100 mil [THT, multilayer]"]
  C3 = Ceramic Capacitor [capacitance="100 nF" package="100 mil [THT, multilayer]"]
  Q5 = NPN-Transistor [part_number=2N2222A package="TO92 [THT]"]
  Q1 = NPN-Transistor [part_number=2N2222A package="TO92 [THT]"]
  R11 = Resistor [tolerance=±5% resistance=1k package=THT]
  Q3 = NPN-Transistor [part_number=2N2222A package="TO92 [THT]"]
  C7 = Ceramic Capacitor [capacitance="100 nF" package="100 mil [THT, multilayer]"]
  C15 = Ceramic Capacitor [capacitance="100 nF" package="100 mil [THT, multilayer]"]
  C1 = Resistor [tolerance=±5% resistance=220 part_number=C-0.47uF package=THT]
  R1 = Resistor [tolerance=±5% resistance=1k package=THT]
  C2 = Electrolytic Capacitor [capacitance=1mF voltage=25V package="200 mil [THT, electrolytic]"]
  C4 = Electrolytic Capacitor [capacitance=0.47mF voltage=10V package="200 mil [THT, electrolytic]"]
  LED1 = LED - 5mm [color="Red (633nm)" package="5 mm [THT]"]
  Pad5 = Pad [width=5 height=1 connect=center]
  S1 = Pushbutton [package="[THT]"]
  JP7 = Header 2 [package=jst-2-pth]
  JP6 = Header 3 [package=jst-3-pth]
  JP8 = Header 4 [package=jst-4-pth]
  SIM800L_20MM = SIM800L_20MM
  J59 = rounded female pin header, 2 pins [form="♀ (female rounded)"]
  R16 = Resistor [tolerance=±5% resistance=3.3k package=THT]
  C17 = Electrolytic Capacitor [capacitance=0.47mF voltage=10V package="200 mil [THT, electrolytic]"]
  C18 = Ceramic Capacitor [capacitance="100 nF" package="100 mil [THT, multilayer]"]
  J61 = rounded female pin header, 2 pins [form="♀ (female rounded)"]
  R17 = Resistor [tolerance=±5% resistance=10k package=THT]
  C19 = Electrolytic Capacitor [capacitance=33µF voltage=10V package="100 mil [THT, electrolytic]"]
  J62 = rounded female pin header, 2 pins [form="♀ (female rounded)"]
  J63 = rounded female pin header, 2 pins [form="♀ (female rounded)"]
  J60 = rounded female pin header, 2 pins [form="♀ (female rounded)"]
  U1 = AVR 10-pin ICSP Header [package="avr icsp"]
  JP9 = Header 2 [package=jst-2-pth]
  R18 = Resistor [tolerance=±5% resistance=10k package=THT]
  Power_plug1 = Power plug
  S3 = SWITCH-DPDT [package=os]
  JP10 = Header 3 [package=jst-3-pth]

nets:
  N1: L293D.Enable_1, L293D.+V, Sensor_IC.VCC, Sensor_IC.AVCC, Sensor_IC.AREF, R7.Pin_1, 7805.OUT, C3.0, C7.1, C15.1, R1.Pin_0, C4.+, JP6.1, SIM800L_20MM.PIN2, C17.+, C18.1, C19.+, U1.2, JP9.2, JP10.1
  N2: L293D.In_1, J62.pin2
  N3: L293D.Out_1_(_Controlled_by_Enable_1_), SLOW_FAST.pin2
  GND: L293D.0V, Sensor_IC.GND, 7805.GND, R3.Pin_1, C5.0, C6.1, C3.1, Q5.E, Q1.E, Q3.E, C7.0, C15.0, C1.Pin_1, C2.-, C4.-, LED1.cathode, Pad5.pad, S1.Pin_1, S1.Pin_2, JP7.1, JP6.2, JP8.1, SIM800L_20MM.PIN_6, C17.-, C18.0, C19.-, U1.4, Power_plug1.GND, JP10.2
  N4: L293D.Out_2_(_Controlled_by_Enable_1_), SLOW_FAST.pin1
  N5: L293D.In_2, J62.pin1
  N6: L293D.+Vmotor, D1.Pin_1, 7805.IN, R5.Pin_0, C1.Pin_0, C2.+, JP10.3
  N7: Sensor_IC.RESET, R7.Pin_0, S1.Pin_3, S1.Pin_4, U1.5
  N8: Sensor_IC.D0_(RX), J59.pin1
  N9: Sensor_IC.D1_(TX), J59.pin2
  N10: Sensor_IC.D2, J63.pin1
  N11: Sensor_IC.D3_(PWM), Sensor_IC.A1, JP6.3
  N12: Sensor_IC.D4, J63.pin2
  N13: Sensor_IC.XLAT1, XTAL.pin_0, C6.0
  N14: Sensor_IC.XLAT2, XTAL.pin_1, C5.1
  N15: Sensor_IC.D5_(PWM), J60.pin1
  N16: Sensor_IC.D6_(PWM), J60.pin2
  N17: Sensor_IC.D7, R18.Pin_1
  N18: Sensor_IC.D8, R2.Pin_1
  N19: Sensor_IC.D9_(PWM), R17.Pin_0
  N20: Sensor_IC.D10_(PWM), R11.Pin_1
  N21: Sensor_IC.D11_(PWM), U1.1
  N22: Sensor_IC.D12, U1.9
  N23: Sensor_IC.D13, U1.7
  N24: Sensor_IC.A0, R4.Pin_0, R5.Pin_1
  N25: Sensor_IC.A2, R8.Pin_0
  N26: Sensor_IC.A3, R8.Pin_1, JP7.2
  N27: Sensor_IC.A4, JP8.4, R16.Pin_1
  N28: Sensor_IC.A5, R16.Pin_0
  N29: D1.Pin_0, S3.2, S3.5
  N30: R3.Pin_0, R2.Pin_0, Q1.B
  N31: R4.Pin_1, Q1.C
  N32: Q5.B, R18.Pin_0
  N33: Q5.C, JP9.1
  N34: R11.Pin_0, Q3.B
  N35: Q3.C, SIM800L_20MM.PIN_8
  N36: R1.Pin_1, LED1.anode
  N37: SIM800L_20MM.PIN_4, J61.pin2
  N38: SIM800L_20MM.PIN_5, J61.pin1
  N39: SIM800L_20MM.PIN_7, R17.Pin_1
  N40: Power_plug1.VCC, S3.3, S3.6

notes:
  12V INPUT
  T-
  TD
  M-
  1
  STX
  SRX
  J3
  C
  MOTOR
  Krishna
  Commander
  TX
  RX
  SLOW
  FAST
